# Fritzing sketch SoccerCar - schem (saved by Fritzing 0.9.3b)
breadboards: 1

parts:
  U2 = atmega328 [package=dip]
  IC1 = L293D [package=THT]
  U3 = Voltage Regulator - 5V [package="TO220 [THT]"]
  S1 = Pushbutton [package="[SMD]"]
  C1 = Ceramic Capacitor [capacitance=100nF package="100 mil [THT, multilayer]"]
  C2 = Ceramic Capacitor [capacitance=100nF package="100 mil [THT, multilayer]"]
  XTAL1 = Crystal [frequency="16 Mhz" package=THT]
  LED1 = LED - 5mm [color="Orange (612nm)" package="5 mm [THT]"]
  R2 = Resistor [tolerance=±5% resistance=10k package=THT]
  D1 = Diode [package=diode-hv]
  C4 = Capacitor [package=cap-pth-small2]
  C5 = Ceramic Capacitor [capacitance=100nF package="100 mil [THT, multilayer]"]
  C6 = Electrolytic Capacitor [capacitance=100μF voltage=50V package="0807 [SMD, electrolytic]"]
  LED2 = LED - 5mm [color="Green (565nm)" package="5 mm [THT]"]
  R3 = Resistor [tolerance=±5% resistance=150 package=THT]
  C7 = Electrolytic Capacitor [capacitance=1µF voltage=50V package="100 mil [THT, electrolytic]"]
  C8 = Capacitor [package=cap-pth-small2]
  M1 = DC Motor
  M2 = DC Motor
  C9 = Capacitor [package=cap-pth-small2]
  D2 = Rectifier Diode [part_number=1N4001 package="300 mil [THT]"]
  F1 = Resettable Fuse PTC [package=ptc]
  VCC4 = Battery block 9V
  BT1 = Bluetooth HC-06u [package=THT]
  R4 = Resistor [tolerance=±5% resistance=150 package=THT]

nets:
  RESET: U2.RESET, S1.Pin_1, S1.Pin_2, R2.Pin_1, D1.A, C9.2
  D3: U2.D3_(PWM), BT1.TXD
  D4: U2.D4, BT1.RXD
  5V: U2.VCC, U2.AVCC, U3.output_voltage, R2.Pin_0, D1.C, C4.2, C5.0, R3.Pin_1, C7.+, C8.1, BT1.VCC, R4.Pin_0
  GND: U2.GND, IC1.0V, U3.GND, S1.Pin_3, S1.Pin_4, C1.1, C2.0, LED1.cathode, C4.1, C5.1, C6.-, LED2.cathode, C7.-, C8.2, C9.1, VCC4.-, BT1.GND
  N1: U2.XLAT1, C1.0, XTAL1.pin_0
  N2: U2.XLAT2, C2.1, XTAL1.pin_1
  D6(EN1): U2.D6_(PWM), IC1.Enable_1
  D7(IN2): U2.D7, IC1.In_1
  D8(IN2): U2.D8, IC1.In_2
  D9(EN2): U2.D9_(PWM), IC1.Enable_2
  D10(IN3): U2.D10_(PWM), IC1.In_3
  D11(IN4): U2.D11_(PWM), IC1.In_4
  D13: U2.D13, LED1.anode, R3.Pin_0
  N3: IC1.Out_1_(_Controlled_by_Enable_1_), M2.pin_2
  N4: IC1.Out_2_(_Controlled_by_Enable_1_), M2.pin_1
  VCC: IC1.+Vmotor, IC1.+V, D2.anode, F1.1
  N5: IC1.Out_3_(_Controlled_by_Enable_2_), M1.pin_2
  N6: IC1.Out_4_(_Controlled_by_Enable_2_), M1.pin_1
  N7: U3.input_voltage, C6.+, D2.cathode
  N8: LED2.anode, R4.Pin_1
  N9: F1.2, VCC4.+

notes:
  해커톤 SoccerCar

custom parts:
  Bluetooth HC-06u: Bluetooth HC-06 - face up, pins down 16.5mm x 37.5mm PCB
